// Logisim project SD_nandpic.circ as structural Verilog: 1 circuit, main circuit main
module main (
);

  wire nand_1_out, nand_2_out, nand_3_out, nand_4_out, nand_5_out, nand_6_out, nand_7_out, nand_8_out,
       undriven, undriven_2, undriven_3, undriven_4;

  nand nand_1 (nand_1_out, undriven_3, undriven_3);
  nand nand_2 (nand_2_out, undriven_4, undriven_4);
  nand nand_3 (nand_3_out, undriven_2, nand_1_out, undriven_4);
  nand nand_4 (nand_4_out, undriven, undriven_3);
  nand nand_5 (nand_5_out, undriven_2, nand_2_out);
  nand nand_6 (nand_6_out, undriven, undriven_4);
  nand nand_7 (nand_7_out, nand_3_out, nand_4_out);
  nand nand_8 (nand_8_out, nand_5_out, nand_6_out);
endmodule
