// Logisim project SD_nor.circ as structural Verilog: 1 circuit, main circuit main
module main (
);

  wire nor_1_out, nor_2_out, nor_3_out, nor_4_out, nor_5_out, nor_6_out, not_1_out, not_2_out, undriven,
       undriven_2, undriven_3, undriven_4;

  not not_1 (not_1_out, undriven_4);
  not not_2 (not_2_out, undriven_2);
  nor nor_1 (nor_1_out, undriven_4, undriven_3);
  nor nor_2 (nor_2_out, undriven, not_1_out);
  nor nor_3 (nor_3_out, undriven, not_2_out);
  nor nor_4 (nor_4_out, undriven_3, undriven_2);
  nor nor_5 (nor_5_out, nor_1_out, undriven_2, nor_2_out);
  nor nor_6 (nor_6_out, nor_3_out, nor_4_out);

  // Notes on the sheet:
  //   1
endmodule
