// Logisim project lab2_sim.circ as structural Verilog: 2 circuits, main circuit main
module main (
  input  in_1,
  input  in_2,
  input  in_3,
  input  in_4,
  input  I0,
  input  I1,
  input  I2
);

  wire controlled_buffer_1_out, n74138_1__3, n74138_2__0, n74138_2__1, n74138_2__2, n74138_2__3, not_1_out,
       not_2_out, not_3_out, not_4_out;
  wire [3:0] not_5_out;

  not not_1 (not_1_out, in_4);
  not not_2 (not_2_out, n74138_1__3);
  not not_3 (not_3_out, I2);
  _74138 u_74138_1 (
    .G1(not_1_out), .nG2a(in_4), .nG2b(in_4), .A(in_1), .B(in_2), .D(in_3), ._3(n74138_1__3));  // open: _0, _1, _2, _4, _5, _6, _7
  assign controlled_buffer_1_out = I2 ? n74138_1__3 : 1'bz;  // Controlled_Buffer controlled_buffer_1
  assign controlled_buffer_1_out = not_3_out ? not_2_out : 1'bz;  // Controlled_Buffer controlled_buffer_2
  not not_4 (not_4_out, controlled_buffer_1_out);
  _74138 u_74138_2 (
    .G1(controlled_buffer_1_out), .nG2a(not_4_out), .nG2b(not_4_out), .A(I0), .B(I1), .D(1'b0),
    ._0(n74138_2__0), ._1(n74138_2__1), ._2(n74138_2__2), ._3(n74138_2__3));  // open: _4, _5, _6, _7
  not not_5 (not_5_out[0], n74138_2__0);
  not not_6 (not_5_out[1], n74138_2__1);
  not not_7 (not_5_out[2], n74138_2__2);
  not not_8 (not_5_out[3], n74138_2__3);
  DotMatrix #(.matrixcols(1), .matrixrows(4)) dotmatrix_1 (.col0(not_5_out));
endmodule

module _74138 (
  input  G1,
  input  nG2a,
  input  nG2b,
  input  A,
  input  B,
  input  D,
  output _0,
  output _1,
  output _2,
  output _3,
  output _4,
  output _5,
  output _6,
  output _7
);

  wire and_1_out, not_1_out;
  wire [7:0] decoder_1_out0;

  not not_1 (not_1_out, G1);
  and and_1 (and_1_out, ~not_1_out, ~nG2a, ~nG2b);  // AND_Gate
  Decoder #(.select(3), .disabled(0)) decoder_1 (
    .out0(decoder_1_out0[0]), .out1(decoder_1_out0[1]), .out2(decoder_1_out0[2]), .out3(decoder_1_out0[3]),
    .out4(decoder_1_out0[4]), .out5(decoder_1_out0[5]), .out6(decoder_1_out0[6]), .out7(decoder_1_out0[7]),
    .sel({D, B, A}), .en(and_1_out));
  assign {_7, _6, _5, _4, _3, _2, _1, _0} = ~decoder_1_out0;  // NOT_Gate not_2, 8 bits wide
endmodule
