// Logisim project lab2scheme.circ as structural Verilog: 2 circuits, main circuit main
module main (
);

  wire controlled_buffer_1_out, n74138_1__3, n74138_2__0, n74138_2__1, n74138_2__2, n74138_2__3, not_1_out,
       not_2_out, not_3_out, not_4_out, not_5_out, not_6_out, undriven, undriven_2, undriven_3, undriven_4,
       undriven_5, undriven_6, undriven_7, undriven_8;

  assign controlled_buffer_1_out = undriven_7 ? n74138_1__3 : 1'bz;  // Controlled_Buffer controlled_buffer_1
  not not_1 (not_1_out, n74138_1__3);
  assign controlled_buffer_1_out = not_2_out ? not_1_out : 1'bz;  // Controlled_Buffer controlled_buffer_2
  not not_2 (not_2_out, undriven_7);
  _74138 u_74138_1 (
    .G1(undriven_8), .nG2a(undriven_3), .nG2b(undriven_3), .A(undriven), .B(undriven_2), .D(undriven_6),
    ._3(n74138_1__3));  // open: _0, _1, _2, _4, _5, _6, _7
  _74138 u_74138_2 (
    .G1(controlled_buffer_1_out), .nG2a(1'b0), .nG2b(1'b0), .A(undriven_4), .B(undriven_5), .D(1'b0),
    ._0(n74138_2__0), ._1(n74138_2__1), ._2(n74138_2__2), ._3(n74138_2__3));  // open: _4, _5, _6, _7
  not not_3 (not_3_out, n74138_2__0);
  not not_4 (not_4_out, n74138_2__1);
  not not_5 (not_5_out, n74138_2__2);
  not not_6 (not_6_out, n74138_2__3);

  // Notes on the sheet:
  //   Vcc
endmodule

module _74138 (
  input  G1,
  input  nG2a,
  input  nG2b,
  input  A,
  input  B,
  input  D,
  output _0,
  output _1,
  output _2,
  output _3,
  output _4,
  output _5,
  output _6,
  output _7
);

  wire and_1_out;
  wire [7:0] decoder_1_out0;

  and and_1 (and_1_out, G1, ~nG2a, ~nG2b);  // AND_Gate
  Decoder #(.select(3), .disabled(0)) decoder_1 (
    .out0(decoder_1_out0[0]), .out1(decoder_1_out0[1]), .out2(decoder_1_out0[2]), .out3(decoder_1_out0[3]),
    .out4(decoder_1_out0[4]), .out5(decoder_1_out0[5]), .out6(decoder_1_out0[6]), .out7(decoder_1_out0[7]),
    .sel({D, B, A}), .en(and_1_out));
  assign {_7, _6, _5, _4, _3, _2, _1, _0} = ~decoder_1_out0;  // NOT_Gate not_1, 8 bits wide
endmodule
